// Logisim project Digital_clock.circ as structural Verilog: 1 circuit, main circuit main
module main (
);

  wire and_1_out, and_2_out, and_3_out, and_4_out, and_5_out, clock_1_out, comparator_1_eq, comparator_2_eq,
       comparator_3_eq, comparator_4_eq, comparator_5_eq, comparator_6_eq, counter_2_carry, counter_3_carry,
       counter_4_carry, counter_5_carry, counter_6_carry, d_ff_1_q, d_ff_2_q, d_ff_3_q, d_ff_4_q, d_ff_5_q;
  wire [3:0] counter_1_q, counter_2_q, counter_3_q, counter_4_q, counter_5_q, counter_6_q;
  wire [6:0] multiplexer_1_out, multiplexer_2_out, multiplexer_3_out, multiplexer_4_out, multiplexer_5_out,
       multiplexer_6_out;

  _7_Segment_Display u_7_segment_display_1 (
    .g(multiplexer_1_out[0]), .f(multiplexer_1_out[6]), .a(multiplexer_1_out[5]), .b(multiplexer_1_out[4]),
    .e(multiplexer_1_out[1]), .d(multiplexer_1_out[2]), .c(multiplexer_1_out[3]));  // open: dp
  Multiplexer #(.select(4), .width(7)) multiplexer_1 (
    .in0(7'b1111110), .in1(7'b0011000), .out(multiplexer_1_out), .sel(counter_1_q));  // open: in2, in3, in4, in5, in6, in7, in8, in9, in10, in11, in12, in13, in14, in15, en
  Counter #(.width(4), .max('h1)) counter_1 (
    .count(d_ff_1_q), .Q(counter_1_q), .clk(clock_1_out), .clr(and_5_out));  // open: load, D, carry
  Comparator #(.width(4), .mode("unsigned")) comparator_1 (
    .a(counter_1_q), .b(4'b0001), .eq(comparator_1_eq));  // open: gt, lt
  Comparator #(.width(4), .mode("unsigned")) comparator_2 (
    .a(counter_2_q), .b(4'b0001), .eq(comparator_2_eq));  // open: gt, lt
  Comparator #(.width(4), .mode("unsigned")) comparator_3 (
    .a(counter_3_q), .b(4'b0101), .eq(comparator_3_eq));  // open: gt, lt
  Comparator #(.width(4), .mode("unsigned")) comparator_4 (
    .a(counter_4_q), .b(4'b1001), .eq(comparator_4_eq));  // open: gt, lt
  Comparator #(.width(4), .mode("unsigned")) comparator_5 (
    .a(counter_5_q), .b(4'b0101), .eq(comparator_5_eq));  // open: gt, lt
  Comparator #(.width(4), .mode("unsigned")) comparator_6 (
    .a(counter_6_q), .b(4'b1001), .eq(comparator_6_eq));  // open: gt, lt
  _7_Segment_Display u_7_segment_display_2 (
    .g(multiplexer_2_out[0]), .f(multiplexer_2_out[6]), .a(multiplexer_2_out[5]), .b(multiplexer_2_out[4]),
    .e(multiplexer_2_out[1]), .d(multiplexer_2_out[2]), .c(multiplexer_2_out[3]));  // open: dp
  Multiplexer #(.select(4), .width(7)) multiplexer_2 (
    .in0(7'b1111110), .in1(7'b0011000), .in2(7'b0110111), .in3(7'b0111101), .in4(7'b1011001),
    .in5(7'b1101101), .in6(7'b1101111), .in7(7'b0111000), .in8({7{1'b1}}), .in9(7'b1111101),
    .out(multiplexer_2_out), .sel(counter_2_q));  // open: in10, in11, in12, in13, in14, in15, en
  Counter #(.width(4), .max('h9)) counter_2 (
    .count(d_ff_2_q), .Q(counter_2_q), .carry(counter_2_carry), .clk(clock_1_out), .clr(and_5_out));  // open: load, D
  D_Flip_Flop #(.trigger("falling")) d_ff_1 (
    .clk(clock_1_out), .D(and_1_out), .Q(d_ff_1_q));  // open: Qn, preset, en, reset
  and and_1 (and_1_out, counter_2_carry, and_2_out);
  Multiplexer #(.select(4), .width(7)) multiplexer_3 (
    .in0(7'b1111110), .in1(7'b0011000), .in2(7'b0110111), .in3(7'b0111101), .in4(7'b1011001),
    .in5(7'b1101101), .out(multiplexer_3_out), .sel(counter_3_q));  // open: in6, in7, in8, in9, in10, in11, in12, in13, in14, in15, en
  Counter #(.width(4), .max('h5)) counter_3 (
    .count(d_ff_3_q), .Q(counter_3_q), .carry(counter_3_carry), .clk(clock_1_out), .clr(and_5_out));  // open: load, D
  D_Flip_Flop #(.trigger("falling")) d_ff_2 (
    .clk(clock_1_out), .D(and_2_out), .Q(d_ff_2_q));  // open: Qn, preset, en, reset
  and and_2 (and_2_out, counter_3_carry, and_3_out);
  _7_Segment_Display u_7_segment_display_3 (
    .g(multiplexer_3_out[0]), .f(multiplexer_3_out[6]), .a(multiplexer_3_out[5]), .b(multiplexer_3_out[4]),
    .e(multiplexer_3_out[1]), .d(multiplexer_3_out[2]), .c(multiplexer_3_out[3]));  // open: dp
  and and_3 (and_3_out, counter_4_carry, and_4_out);
  _7_Segment_Display u_7_segment_display_4 (
    .g(multiplexer_4_out[0]), .f(multiplexer_4_out[6]), .a(multiplexer_4_out[5]), .b(multiplexer_4_out[4]),
    .e(multiplexer_4_out[1]), .d(multiplexer_4_out[2]), .c(multiplexer_4_out[3]));  // open: dp
  Multiplexer #(.select(4), .width(7)) multiplexer_4 (
    .in0(7'b1111110), .in1(7'b0011000), .in2(7'b0110111), .in3(7'b0111101), .in4(7'b1011001),
    .in5(7'b1101101), .in6(7'b1101111), .in7(7'b0111000), .in8({7{1'b1}}), .in9(7'b1111101),
    .out(multiplexer_4_out), .sel(counter_4_q));  // open: in10, in11, in12, in13, in14, in15, en
  Counter #(.width(4), .max('h9)) counter_4 (
    .count(d_ff_4_q), .Q(counter_4_q), .carry(counter_4_carry), .clk(clock_1_out), .clr(and_5_out));  // open: load, D
  D_Flip_Flop #(.trigger("falling")) d_ff_3 (
    .clk(clock_1_out), .D(and_3_out), .Q(d_ff_3_q));  // open: Qn, preset, en, reset
  and and_4 (and_4_out, counter_5_carry, counter_6_carry);
  and and_5 (and_5_out, comparator_1_eq, comparator_2_eq, comparator_3_eq, comparator_4_eq, comparator_5_eq, comparator_6_eq);
  Counter #(.width(4), .max('h5)) counter_5 (
    .count(d_ff_5_q), .Q(counter_5_q), .carry(counter_5_carry), .clk(clock_1_out), .clr(and_5_out));  // open: load, D
  D_Flip_Flop #(.trigger("falling")) d_ff_4 (
    .clk(clock_1_out), .D(and_4_out), .Q(d_ff_4_q));  // open: Qn, preset, en, reset
  _7_Segment_Display u_7_segment_display_5 (
    .g(multiplexer_5_out[0]), .f(multiplexer_5_out[6]), .a(multiplexer_5_out[5]), .b(multiplexer_5_out[4]),
    .e(multiplexer_5_out[1]), .d(multiplexer_5_out[2]), .c(multiplexer_5_out[3]));  // open: dp
  Multiplexer #(.select(4), .width(7)) multiplexer_5 (
    .in0(7'b1111110), .in1(7'b0011000), .in2(7'b0110111), .in3(7'b0111101), .in4(7'b1011001),
    .in5(7'b1101101), .out(multiplexer_5_out), .sel(counter_5_q));  // open: in6, in7, in8, in9, in10, in11, in12, in13, in14, in15, en
  Counter #(.width(4), .max('h9)) counter_6 (
    .Q(counter_6_q), .carry(counter_6_carry), .clk(clock_1_out), .clr(and_5_out));  // open: load, D, count
  Clock clock_1 (.out(clock_1_out));
  D_Flip_Flop #(.trigger("falling")) d_ff_5 (
    .clk(clock_1_out), .D(counter_6_carry), .Q(d_ff_5_q));  // open: Qn, preset, en, reset
  _7_Segment_Display u_7_segment_display_6 (
    .g(multiplexer_6_out[0]), .f(multiplexer_6_out[6]), .a(multiplexer_6_out[5]), .b(multiplexer_6_out[4]),
    .e(multiplexer_6_out[1]), .d(multiplexer_6_out[2]), .c(multiplexer_6_out[3]));  // open: dp
  Multiplexer #(.select(4), .width(7)) multiplexer_6 (
    .in0(7'b1111110), .in1(7'b0011000), .in2(7'b0110111), .in3(7'b0111101), .in4(7'b1011001),
    .in5(7'b1101101), .in6(7'b1101111), .in7(7'b0111000), .in8({7{1'b1}}), .in9(7'b1111101),
    .out(multiplexer_6_out), .sel(counter_6_q));  // open: in10, in11, in12, in13, in14, in15, en
endmodule
