// Logisim project HERA_microprocessor.circ as structural Verilog: 12 circuits, main circuit main
// 2
module main (
  output [15:0] Registers,
  output [15:0] out_2,
  output [15:0] out_3,
  output [15:0] out_4,
  output [15:0] out_5,
  output [15:0] out_6,
  output [15:0] out_7,
  output [15:0] out_8,
  output [15:0] out_9,
  output [15:0] out_10,
  output [15:0] out_11,
  output [15:0] out_12,
  output [15:0] out_13,
  output [15:0] out_14,
  output [15:0] out_15,
  output [15:0] out_16,
  output [4:0] Flags
);

  wire and_2_out, and_3_out, b_1_out_11, clock_1_out, comparator_1_lt, Ld, M, multiplexer_13_out,
       operation_control_1_halt, operation_control_1_out_8, operation_control_1_out_12,
       operation_control_1_out_14, operation_control_1_out_18, operation_control_1_out_26,
       operation_control_1_relative_branch, St;
  wire [1:0] operation_control_1_out_17;
  wire [2:0] operation_control_1_out_15;
  wire [3:0] _1, _2, A, A_prime, b_1_out_9, operation_control_1_out_3, operation_control_1_out_4,
       operation_control_1_out_10, operation_control_1_out_13, operation_control_1_out_16_2,
       operation_control_1_rb, operation_control_1_rd, S1, S2;
  wire [4:0] a_1_out_3, alsu_1_out_8, and_1_out, multiplexer_6_out, multiplexer_7_out, multiplexer_8_out,
       multiplexer_9_out, not_1_out, or_1_out, OS, register_file_1_out_6;
  wire [4:4] operation_control_1_out_16;
  wire [5:0] operation_control_1_out_11;
  wire [7:0] operation_control_1_out_7, register_file_1_out_7;
  wire [10:0] register_file_1_out_6_2;
  wire [15:0] adder_1_out, adder_2_out, alsu_1_out_7, B, b_1_out_10, B_prime, bit_extender_1_out,
       bit_extender_2_out, branching_control_1_out_7, multiplexer_1_out, multiplexer_2_out,
       multiplexer_5_out, multiplexer_11_out, PC, ram_1_data, register_1_q, rom_1_data;
  wire [15:8] register_file_1_out_7_2;

  Operation_Control operation_control_1 (
    .in_1(rom_1_data), .HALT(operation_control_1_halt), .out_3(operation_control_1_out_3),
    .out_4(operation_control_1_out_4), .out_5(S1), .Source_2(S2), .out_7(operation_control_1_out_7),
    .out_8(operation_control_1_out_8), .out_9(operation_control_1_out_17[1]),
    .out_10(operation_control_1_out_10), .out_11(operation_control_1_out_11),
    .out_12(operation_control_1_out_12), .out_13(operation_control_1_out_13),
    .out_14(operation_control_1_out_14), .out_15(operation_control_1_out_15),
    .out_16({operation_control_1_out_16[4], operation_control_1_out_16_2}),
    .out_17(operation_control_1_out_17[0]), .out_18(operation_control_1_out_18),
    .relative_branch(operation_control_1_relative_branch), .STORE(St), .out_21(Ld), .out_22(M), .out_23(OS),
    .Rd(operation_control_1_rd), .Rb(operation_control_1_rb), .out_26(operation_control_1_out_26));
  assign not_1_out = ~{operation_control_1_out_16[4], operation_control_1_out_16_2};  // NOT_Gate not_1, 5 bits wide
  Comparator comparator_1 (.a(operation_control_1_out_7), .b({8{1'b0}}), .lt(comparator_1_lt));  // open: gt, eq
  Multiplexer #(.width(16)) multiplexer_1 (
    .in0(multiplexer_2_out), .in1({operation_control_1_out_7, register_file_1_out_7}),
    .out(multiplexer_1_out), .sel(operation_control_1_out_8));  // open: en
  Multiplexer #(.width(16)) multiplexer_2 (
    .in0({{8{1'b0}}, operation_control_1_out_7}), .in1({{8{1'b1}}, operation_control_1_out_7}),
    .out(multiplexer_2_out), .sel(comparator_1_lt));  // open: en
  assign or_1_out = {operation_control_1_out_16[4], operation_control_1_out_16_2} | Flags;  // OR_Gate or_1, 5 bits wide
  assign and_1_out = Flags & not_1_out;  // AND_Gate and_1, 5 bits wide
  ROM #(.addrWidth(16), .dataWidth(16)) rom_1 (.addr(PC), .data(rom_1_data));  // open: sel
  A a_1 (.in_1(ram_1_data), .in_2(Flags), .out_3(a_1_out_3));
  Multiplexer #(.width(4)) multiplexer_3 (.in0(S1), .in1(operation_control_1_rd), .out(_1), .sel(M));  // open: en
  Multiplexer #(.width(4)) multiplexer_4 (.in0(S2), .in1(operation_control_1_rb), .out(_2), .sel(M));  // open: en
  PC_register pc_register_1 (
    .HALT(operation_control_1_halt), .Clock(multiplexer_13_out), .out_5(PC),
    .in_3(operation_control_1_out_12), .in_4(multiplexer_5_out));
  Multiplexer #(.width(16)) multiplexer_5 (
    .in0(branching_control_1_out_7), .in1(register_1_q), .out(multiplexer_5_out),
    .sel(operation_control_1_out_26));  // open: en
  Multiplexer #(.width(5)) multiplexer_6 (
    .in0(multiplexer_9_out), .in1(a_1_out_3), .out(multiplexer_6_out), .sel(Ld));  // open: en
  Flags flags_1 (.in_1(multiplexer_6_out), .Clock(multiplexer_13_out), .out_3(Flags));
  ALSU alsu_1 (
    .in_1({register_file_1_out_6_2, register_file_1_out_6}),
    .in_2({register_file_1_out_7_2, register_file_1_out_7}), .Operation_Select(operation_control_1_out_3),
    .in_4(Flags), .out_7(alsu_1_out_7), .out_8(alsu_1_out_8), .SHift_OP(operation_control_1_out_10),
    .Inc_Dec(operation_control_1_out_11));
  Multiplexer #(.width(5)) multiplexer_7 (
    .in0(alsu_1_out_8), .in1(multiplexer_8_out), .out(multiplexer_7_out), .sel(operation_control_1_out_14));  // open: en
  Multiplexer #(.select(3), .width(5)) multiplexer_8 (
    .in0(or_1_out), .in2({1'b0, operation_control_1_out_16_2}), .in4(and_1_out),
    .in6({operation_control_1_out_16[4], operation_control_1_out_16_2}), .out(multiplexer_8_out),
    .sel(operation_control_1_out_15));  // open: in1, in3, in5, in7, en
  assign bit_extender_1_out = {{11{1'b0}}, Flags};  // Bit_Extender bit_extender_1
  Multiplexer #(.width(5)) multiplexer_9 (
    .in0(multiplexer_7_out), .in1(register_file_1_out_6), .out(multiplexer_9_out),
    .sel(operation_control_1_out_18));  // open: en
  Multiplexer #(.width(4)) multiplexer_10 (
    .in0(operation_control_1_out_4), .in1(operation_control_1_rd), .out(A), .sel(Ld));  // open: en
  Multiplexer #(.select(2), .width(16)) multiplexer_11 (
    .in0(alsu_1_out_7), .in1(bit_extender_1_out), .in2(multiplexer_1_out), .out(multiplexer_11_out),
    .sel(operation_control_1_out_17));  // open: in3, en
  Multiplexer #(.width(16)) multiplexer_12 (.in0(multiplexer_11_out), .in1(ram_1_data), .out(B), .sel(Ld));  // open: en
  Adder #(.width(16)) adder_1 (.a(PC), .b(16'h1), .out(adder_1_out));  // open: cin, cout
  Branching_Control branching_control_1 (
    .in_1(PC), .in_2(operation_control_1_out_7), .BCVZS(Flags),
    .in_4({register_file_1_out_7_2, register_file_1_out_7}), .in_5(operation_control_1_relative_branch),
    .in_6(operation_control_1_out_13), .out_7(branching_control_1_out_7));
  Register_File register_file_1 (
    .in_4(B_prime), .Clock(clock_1_out), .out_6({register_file_1_out_6_2, register_file_1_out_6}),
    .out_7({register_file_1_out_7_2, register_file_1_out_7}), .out_8(Registers), .out_9(out_2),
    .out_10(out_3), .out_11(out_4), .out_12(out_5), .out_13(out_6), .out_14(out_7), .out_15(out_8),
    .out_16(out_9), .out_17(out_10), .out_18(out_11), .out_19(out_12), .out_20(out_13), .out_21(out_14),
    .out_22(out_15), .out_23(out_16), .in_1(A_prime), .in_2(_1), .in_3(_2));
  Clock clock_1 (.out(clock_1_out));
  assign bit_extender_2_out = {{11{1'b0}}, OS};  // Bit_Extender bit_extender_2
  B b_1 (
    .in_1(S2), .in_2(4'b1110), .in_3(S1), .in_4(adder_1_out),
    .in_5({register_file_1_out_6_2, register_file_1_out_6}),
    .in_6({register_file_1_out_7_2, register_file_1_out_7}), .in_7(clock_1_out),
    .in_8(operation_control_1_out_26), .out_9(b_1_out_9), .out_10(b_1_out_10), .out_11(b_1_out_11));
  and and_2 (and_2_out, clock_1_out, b_1_out_11);
  Adder #(.width(16)) adder_2 (
    .a({register_file_1_out_7_2, register_file_1_out_7}), .b(bit_extender_2_out), .out(adder_2_out));  // open: cin, cout
  Register #(.width(16)) register_1 (.D(out_14), .Q(register_1_q), .clk(multiplexer_13_out));  // open: en, clr
  Multiplexer multiplexer_13 (
    .in0(clock_1_out), .in1(and_2_out), .out(multiplexer_13_out), .sel(operation_control_1_out_26));  // open: en
  and and_3 (and_3_out, St, multiplexer_13_out);
  Multiplexer #(.width(4)) multiplexer_14 (
    .in0(A), .in1(b_1_out_9), .out(A_prime), .sel(operation_control_1_out_26));  // open: en
  Multiplexer #(.width(16)) multiplexer_15 (
    .in0(B), .in1(b_1_out_10), .out(B_prime), .sel(operation_control_1_out_26));  // open: en
  RAM #(.dataWidth(16), .bus("separate")) ram_1 (
    .addr(adder_2_out[7:0]), .din({register_file_1_out_6_2, register_file_1_out_6}), .data(ram_1_data),
    .clk(and_3_out));  // open: str, sel, ld, clr
  Hex_Digit_Display hex_digit_display_1 (.value(Registers[11:8]));  // open: dp
  Hex_Digit_Display hex_digit_display_2 (.value(Registers[15:12]));  // open: dp
  Hex_Digit_Display hex_digit_display_3 (.value(out_2[15:12]));  // open: dp
  Hex_Digit_Display hex_digit_display_4 (.value(out_2[11:8]));  // open: dp
  Hex_Digit_Display hex_digit_display_5 (.value(out_3[15:12]));  // open: dp
  Hex_Digit_Display hex_digit_display_6 (.value(out_3[11:8]));  // open: dp
  Hex_Digit_Display hex_digit_display_7 (.value(out_4[15:12]));  // open: dp
  Hex_Digit_Display hex_digit_display_8 (.value(out_4[11:8]));  // open: dp
  Hex_Digit_Display hex_digit_display_9 (.value(out_5[11:8]));  // open: dp
  Hex_Digit_Display hex_digit_display_10 (.value(out_5[15:12]));  // open: dp
  Hex_Digit_Display hex_digit_display_11 (.value(out_6[15:12]));  // open: dp
  Hex_Digit_Display hex_digit_display_12 (.value(out_6[11:8]));  // open: dp
  Hex_Digit_Display hex_digit_display_13 (.value(out_7[11:8]));  // open: dp
  Hex_Digit_Display hex_digit_display_14 (.value(out_7[15:12]));  // open: dp
  Hex_Digit_Display hex_digit_display_15 (.value(out_8[11:8]));  // open: dp
  Hex_Digit_Display hex_digit_display_16 (.value(out_8[15:12]));  // open: dp
  Hex_Digit_Display hex_digit_display_17 (.value(out_9[11:8]));  // open: dp
  Hex_Digit_Display hex_digit_display_18 (.value(out_9[15:12]));  // open: dp
  Hex_Digit_Display hex_digit_display_19 (.value(out_10[15:12]));  // open: dp
  Hex_Digit_Display hex_digit_display_20 (.value(out_10[11:8]));  // open: dp
  Hex_Digit_Display hex_digit_display_21 (.value(out_11[15:12]));  // open: dp
  Hex_Digit_Display hex_digit_display_22 (.value(out_11[11:8]));  // open: dp
  Hex_Digit_Display hex_digit_display_23 (.value(Registers[7:4]));  // open: dp
  Hex_Digit_Display hex_digit_display_24 (.value(Registers[3:0]));  // open: dp
  Hex_Digit_Display hex_digit_display_25 (.value(out_2[3:0]));  // open: dp
  Hex_Digit_Display hex_digit_display_26 (.value(out_2[7:4]));  // open: dp
  Hex_Digit_Display hex_digit_display_27 (.value(out_3[3:0]));  // open: dp
  Hex_Digit_Display hex_digit_display_28 (.value(out_3[7:4]));  // open: dp
  Hex_Digit_Display hex_digit_display_29 (.value(out_4[3:0]));  // open: dp
  Hex_Digit_Display hex_digit_display_30 (.value(out_4[7:4]));  // open: dp
  Hex_Digit_Display hex_digit_display_31 (.value(out_5[7:4]));  // open: dp
  Hex_Digit_Display hex_digit_display_32 (.value(out_5[3:0]));  // open: dp
  Hex_Digit_Display hex_digit_display_33 (.value(out_6[3:0]));  // open: dp
  Hex_Digit_Display hex_digit_display_34 (.value(out_6[7:4]));  // open: dp
  Hex_Digit_Display hex_digit_display_35 (.value(out_7[3:0]));  // open: dp
  Hex_Digit_Display hex_digit_display_36 (.value(out_7[7:4]));  // open: dp
  Hex_Digit_Display hex_digit_display_37 (.value(out_8[3:0]));  // open: dp
  Hex_Digit_Display hex_digit_display_38 (.value(out_8[7:4]));  // open: dp
  Hex_Digit_Display hex_digit_display_39 (.value(out_9[3:0]));  // open: dp
  Hex_Digit_Display hex_digit_display_40 (.value(out_9[7:4]));  // open: dp
  Hex_Digit_Display hex_digit_display_41 (.value(out_10[3:0]));  // open: dp
  Hex_Digit_Display hex_digit_display_42 (.value(out_10[7:4]));  // open: dp
  Hex_Digit_Display hex_digit_display_43 (.value(out_11[7:4]));  // open: dp
  Hex_Digit_Display hex_digit_display_44 (.value(out_11[3:0]));  // open: dp

  // Notes on the sheet:
  //   Op Control
  //   Program ROM
  //   lo
  //   hi
  //   contents of rom_1 (hex, n*v repeats v):
  //   e1ff f1ff e201 f200 3068 6154 6224 4354 4424 34c3 3384 b143 3184 eb12 fb00 1a0b 8114 0 ed15 fd00
  //   20cd a334 3384 3303 d113
  //   PC Register
  //   FLags
  //   ALSU
  //   Register File
  //   R0
  //   R1
  //   R2
  //   R3
  //   R4
  //   R5
  //   R6
  //   R7
  //   R8
  //   R9
  //   R10
  //   R11
  //   R12
  //   R13
  //   R14
  //   R15
  //   BCVZS
  //   R0
  //   R1
  //   R2
  //   R3
  //   R4
  //   R5
  //   R6
  //   R7
  //   R8
  //   R9
  //   R10
endmodule

module PC_register (
  input  HALT,
  input  Clock,
  input  in_3,
  input  [15:0] in_4,
  output [15:0] out_5
);

  wire multiplexer_1_out, multiplexer_2_out, not_1_out;

  Multiplexer multiplexer_1 (.in0(in_3), .in1(1'b0), .out(multiplexer_1_out), .sel(HALT));  // open: en
  not not_1 (not_1_out, in_3);
  Multiplexer multiplexer_2 (.in0(not_1_out), .in1(1'b0), .out(multiplexer_2_out), .sel(HALT));  // open: en
  Counter #(.width(16), .max('hffff)) counter_1 (
    .load(multiplexer_1_out), .D(in_4), .count(multiplexer_2_out), .Q(out_5), .clk(Clock));  // open: carry, clr

  // Notes on the sheet:
  //   branching
  //   Program Line Number
endmodule

module Register_File (
  input  [3:0] in_1,
  input  [3:0] in_2,
  input  [3:0] in_3,
  input  [15:0] in_4,
  input  Clock,
  output [15:0] out_6,
  output [15:0] out_7,
  output [15:0] out_8,
  output [15:0] out_9,
  output [15:0] out_10,
  output [15:0] out_11,
  output [15:0] out_12,
  output [15:0] out_13,
  output [15:0] out_14,
  output [15:0] out_15,
  output [15:0] out_16,
  output [15:0] out_17,
  output [15:0] out_18,
  output [15:0] out_19,
  output [15:0] out_20,
  output [15:0] out_21,
  output [15:0] out_22,
  output [15:0] out_23
);

  _2_port_RAM u_2_port_ram_1 (
    .WA(in_1), .Clock(Clock), .out_6(out_6), .out_7(out_7), .out_8(out_8), .out_9(out_9), .out_10(out_10),
    .out_11(out_11), .out_12(out_12), .out_13(out_13), .out_14(out_14), .out_15(out_15), .out_16(out_16),
    .out_17(out_17), .out_18(out_18), .out_19(out_19), .out_20(out_20), .out_21(out_21), .out_22(out_22),
    .out_23(out_23), .in_1(in_2), .in_2(in_3), .in_4(in_4));

  // Notes on the sheet:
  //   Register Adresses
  //   Result from ALSU
  //   Source Register Data
  //   Operand 1
  //   Operand 2
  //   R0
  //   R1
  //   R2
  //   R3
  //   R4
  //   R5
  //   R6
  //   R7
  //   R8
  //   R9
  //   R10
  //   R11
  //   R12
  //   R13
  //   R14
  //   R15
endmodule

module ALSU (
  input  [15:0] in_1,
  input  [15:0] in_2,
  input  [3:0] Operation_Select,
  input  [4:0] in_4,
  input  [3:0] SHift_OP,
  input  [5:0] Inc_Dec,
  output [15:0] out_7,
  output [4:0] out_8
);

  wire adder_2_cout, adder_3_cout, and_1_out, and_3_out, and_4_out, and_5_out, and_6_out, and_7_out,
       and_8_out, comparator_1_gt, comparator_1_lt, comparator_2_gt, comparator_2_lt, comparator_3_eq,
       comparator_4_gt, comparator_4_lt, comparator_5_gt, comparator_5_lt, comparator_6_gt, comparator_6_lt,
       comparator_7_gt, comparator_7_lt, comparator_8_gt, comparator_8_lt, multiplexer_2_out,
       multiplexer_3_out, multiplexer_7_out, multiplexer_9_out, not_1_out, not_2_out, not_3_out, not_4_out,
       not_5_out, not_6_out, not_7_out, not_8_out, or_2_out, or_3_out, or_4_out, subtractor_1_bout,
       subtractor_2_bout;
  wire [0:0] multiplexer_1_out;
  wire [5:0] adder_1_out;
  wire [15:0] adder_2_out, adder_3_out, adder_4_out, and_2_out, bit_extender_1_out, multiplexer_4_out,
       multiplexer_5_out, multiplier_1_cout, multiplier_1_out, or_1_out, shifter_1_out, shifter_2_out,
       shifter_3_out, shifter_4_out, shifter_5_out, shifter_6_out, subtractor_1_out, subtractor_2_out,
       undriven, xor_1_out;

  and and_1 (and_1_out, in_4[0], not_1_out);
  not not_1 (not_1_out, in_4[4]);
  Multiplexer multiplexer_1 (.in0(in_4[3]), .in1(1'b0), .out(multiplexer_1_out[0]), .sel(in_4[4]));  // open: en
  Shifter #(.width(16)) shifter_1 (.in(in_2), .\dist (4'b0001), .out(shifter_1_out));
  Adder #(.width(6)) adder_1 (.a(Inc_Dec), .b(6'b000001), .out(adder_1_out));  // open: cin, cout
  Shifter #(.width(16), .shift("lr")) shifter_2 (.in(in_2), .\dist (4'b0001), .out(shifter_2_out));
  Shifter #(.width(16)) shifter_3 (.in(in_2), .\dist (4'b1000), .out(shifter_3_out));
  Shifter #(.width(16), .shift("lr")) shifter_4 (.in(in_2), .\dist (4'b1000), .out(shifter_4_out));
  Shifter #(.width(16)) shifter_5 (.in(in_2), .\dist (4'b0001), .out(shifter_5_out));
  Shifter #(.width(16), .shift("ar")) shifter_6 (.in(in_2), .\dist (4'b0001), .out(shifter_6_out));
  assign bit_extender_1_out = {{10{1'b0}}, adder_1_out};  // Bit_Extender bit_extender_1
  Multiplexer multiplexer_2 (.in0(in_4[3]), .in1(1'b0), .out(multiplexer_2_out), .sel(in_4[4]));  // open: en
  not not_2 (not_2_out, in_4[3]);
  Multiplier #(.width(16)) multiplier_1 (
    .a(in_1), .b(in_2), .out(multiplier_1_out), .cout(multiplier_1_cout));  // open: cin
  Adder #(.width(16)) adder_2 (.a(in_2), .b(bit_extender_1_out), .out(adder_2_out), .cout(adder_2_cout));  // open: cin
  Subtractor #(.width(16)) subtractor_1 (
    .a(in_2), .b(bit_extender_1_out), .out(subtractor_1_out), .bout(subtractor_1_bout));  // open: bin
  Adder #(.width(16)) adder_3 (.a(in_1), .b(in_2), .out(adder_3_out), .cin(multiplexer_2_out), .cout(adder_3_cout));
  Multiplexer multiplexer_3 (.in0(not_2_out), .in1(1'b0), .out(multiplexer_3_out), .sel(in_4[4]));  // open: en
  Subtractor #(.width(16)) subtractor_2 (
    .a(in_1), .b(in_2), .out(subtractor_2_out), .bin(multiplexer_3_out), .bout(subtractor_2_bout));
  Multiplexer #(.width(16)) multiplexer_4 (
    .in0(multiplier_1_out), .in1(multiplier_1_cout), .out(multiplexer_4_out), .sel(and_1_out));  // open: en
  assign and_2_out = in_1 & in_2;  // AND_Gate and_2, 16 bits wide
  assign or_1_out = in_1 | in_2;  // OR_Gate or_1, 16 bits wide
  assign xor_1_out = in_1 ^ in_2;  // XOR_Gate xor_1, 16 bits wide
  not not_3 (not_3_out, subtractor_1_bout);
  not not_4 (not_4_out, subtractor_2_bout);
  Adder #(.width(16)) adder_4 (.a(in_2), .b(in_2), .out(adder_4_out), .cin(in_4[3]));  // open: cout
  Multiplexer #(.select(4), .width(16)) multiplexer_5 (
    .in0({shifter_1_out[15:1], multiplexer_1_out[0]}), .in1({multiplexer_1_out[0], shifter_2_out[14:0]}),
    .in2(shifter_3_out), .in3(shifter_4_out), .in4({shifter_5_out[15:1], multiplexer_1_out[0]}),
    .in5(shifter_6_out), .in6(undriven), .in8(adder_2_out), .in9(adder_2_out), .in10(adder_2_out),
    .in11(adder_2_out), .in12(subtractor_1_out), .in13(subtractor_1_out), .in14(subtractor_1_out),
    .in15(subtractor_1_out), .out(multiplexer_5_out), .sel(SHift_OP));  // open: in7, en
  Comparator #(.width(16)) comparator_1 (
    .a(adder_4_out), .b({16{1'b0}}), .gt(comparator_1_gt), .lt(comparator_1_lt));  // open: eq
  Comparator #(.width(16)) comparator_2 (
    .a(in_2), .b({16{1'b0}}), .gt(comparator_2_gt), .lt(comparator_2_lt));  // open: eq
  Multiplexer #(.select(4), .width(16)) multiplexer_6 (
    .in3(multiplexer_5_out), .in8(and_2_out), .in9(or_1_out), .in10(adder_3_out), .in11(subtractor_2_out),
    .in12(multiplexer_4_out), .in13(xor_1_out), .out(out_7), .sel(Operation_Select));  // open: in0, in1, in2, in4, in5, in6, in7, in14, in15, en
  Comparator #(.width(16)) comparator_3 (.a(multiplier_1_cout), .b({16{1'b0}}), .eq(comparator_3_eq));  // open: gt, lt
  Multiplexer #(.select(4)) multiplexer_7 (
    .in0(in_2[15]), .in1(in_2[0]), .in2(in_4[3]), .in3(in_4[3]), .in4(in_2[15]), .in5(in_2[0]),
    .in8(adder_2_cout), .in9(adder_2_cout), .in10(adder_2_cout), .in11(adder_2_cout), .in12(not_3_out),
    .in13(not_3_out), .in14(not_3_out), .in15(not_3_out), .out(multiplexer_7_out), .sel(SHift_OP));  // open: in6, in7, en
  and and_3 (and_3_out, comparator_1_lt, comparator_2_lt);
  Comparator #(.width(16)) comparator_4 (
    .a(out_7), .b({16{1'b0}}), .gt(comparator_4_gt), .eq(out_8[1]), .lt(comparator_4_lt));
  Comparator #(.width(16)) comparator_5 (
    .a(in_1), .b({16{1'b0}}), .gt(comparator_5_gt), .lt(comparator_5_lt));  // open: eq
  Comparator #(.width(16)) comparator_6 (
    .a(in_2), .b({16{1'b0}}), .gt(comparator_6_gt), .lt(comparator_6_lt));  // open: eq
  not not_5 (not_5_out, comparator_3_eq);
  and and_4 (and_4_out, comparator_1_gt, comparator_2_gt);
  or or_2 (or_2_out, and_4_out, and_3_out);
  Comparator #(.width(16)) comparator_7 (
    .a(in_2), .b({16{1'b0}}), .gt(comparator_7_gt), .lt(comparator_7_lt));  // open: eq
  Comparator #(.width(16)) comparator_8 (
    .a(out_7), .b({16{1'b0}}), .gt(comparator_8_gt), .lt(comparator_8_lt));  // open: eq
  and and_5 (and_5_out, comparator_4_gt, comparator_5_gt, comparator_6_gt);
  and and_6 (and_6_out, comparator_4_lt, comparator_5_lt, comparator_6_lt);
  Multiplexer #(.select(4)) multiplexer_8 (
    .in3(multiplexer_7_out), .in8(in_4[3]), .in9(in_4[3]), .in10(adder_3_cout), .in11(not_4_out),
    .in12(not_5_out), .in13(in_4[3]), .out(out_8[3]), .sel(Operation_Select));  // open: in0, in1, in2, in4, in5, in6, in7, in14, in15, en
  Multiplexer #(.select(4)) multiplexer_9 (
    .in0(in_4[2]), .in1(in_4[2]), .in2(in_4[2]), .in3(in_4[2]), .in4(not_6_out), .in5(in_4[2]),
    .in8(not_8_out), .in9(not_8_out), .in10(not_8_out), .in11(not_8_out), .in12(not_8_out), .in13(not_8_out),
    .in14(not_8_out), .in15(not_8_out), .out(multiplexer_9_out), .sel(SHift_OP));  // open: in6, in7, en
  not not_6 (not_6_out, or_2_out);
  not not_7 (not_7_out, or_3_out);
  or or_3 (or_3_out, and_5_out, and_6_out);
  and and_7 (and_7_out, comparator_7_lt, comparator_8_lt);
  Multiplexer #(.select(4)) multiplexer_10 (
    .in3(multiplexer_9_out), .in8(in_4[2]), .in9(in_4[2]), .in10(not_7_out), .in11(not_7_out),
    .in12(not_7_out), .in13(in_4[2]), .out(out_8[2]), .sel(Operation_Select));  // open: in0, in1, in2, in4, in5, in6, in7, in14, in15, en
  and and_8 (and_8_out, comparator_7_gt, comparator_8_gt);
  or or_4 (or_4_out, and_8_out, and_7_out);
  not not_8 (not_8_out, or_4_out);

  assign {out_8[4], out_8[0]} = {in_4[4], out_7[15]};

  // Other names for the same wires on the sheet: Result[15:0] = out_7

  // Notes on the sheet:
  //   Operands
  //   BCVZS
  //   Current Flags
  //   c for shift/inc/dec
  //   C flag
  //   V flag
  //   V for shift/inc/dec
  //   BCVZS
endmodule

module _2_port_RAM (
  input  [3:0] in_1,
  input  [3:0] in_2,
  input  [3:0] WA,
  input  [15:0] in_4,
  input  Clock,
  output [15:0] out_6,
  output [15:0] out_7,
  output [15:0] out_8,
  output [15:0] out_9,
  output [15:0] out_10,
  output [15:0] out_11,
  output [15:0] out_12,
  output [15:0] out_13,
  output [15:0] out_14,
  output [15:0] out_15,
  output [15:0] out_16,
  output [15:0] out_17,
  output [15:0] out_18,
  output [15:0] out_19,
  output [15:0] out_20,
  output [15:0] out_21,
  output [15:0] out_22,
  output [15:0] out_23
);

  wire decoder_1_out0, decoder_1_out1, decoder_1_out2, decoder_1_out3, decoder_1_out4, decoder_1_out5,
       decoder_1_out6, decoder_1_out7, decoder_1_out8, decoder_1_out9, decoder_1_out10, decoder_1_out11,
       decoder_1_out12, decoder_1_out13, decoder_1_out14, decoder_1_out15, decoder_2_out0, decoder_2_out1,
       decoder_2_out2, decoder_2_out3, decoder_2_out4, decoder_2_out5, decoder_2_out6, decoder_2_out7,
       decoder_2_out8, decoder_2_out9, decoder_2_out10, decoder_2_out11, decoder_2_out12, decoder_2_out13,
       decoder_2_out14, decoder_2_out15, decoder_3_out0, decoder_3_out1, decoder_3_out2, decoder_3_out3,
       decoder_3_out4, decoder_3_out5, decoder_3_out6, decoder_3_out7, decoder_3_out8, decoder_3_out9,
       decoder_3_out10, decoder_3_out11, decoder_3_out12, decoder_3_out13, decoder_3_out14, decoder_3_out15;
  wire [15:0] memory_cell_1_out_5, memory_cell_2_out_5, memory_cell_3_out_5, memory_cell_4_out_5,
       memory_cell_5_out_5, memory_cell_6_out_5, memory_cell_7_out_5, memory_cell_8_out_5,
       memory_cell_9_out_5, memory_cell_10_out_5, memory_cell_11_out_5, memory_cell_12_out_5,
       memory_cell_13_out_5, memory_cell_14_out_5, memory_cell_15_out_5, memory_cell_16_out_5,
       memory_cell_17_out_5, memory_cell_18_out_5, memory_cell_19_out_5, memory_cell_20_out_5,
       memory_cell_21_out_5, memory_cell_22_out_5, memory_cell_23_out_5, memory_cell_24_out_5,
       memory_cell_25_out_5, memory_cell_26_out_5, memory_cell_27_out_5, memory_cell_28_out_5,
       memory_cell_29_out_5, memory_cell_30_out_5, memory_cell_31_out_5, memory_cell_32_out_5;

  Decoder #(.select(4)) decoder_1 (
    .out0(decoder_1_out0), .out1(decoder_1_out1), .out2(decoder_1_out2), .out3(decoder_1_out3),
    .out4(decoder_1_out4), .out5(decoder_1_out5), .out6(decoder_1_out6), .out7(decoder_1_out7),
    .out8(decoder_1_out8), .out9(decoder_1_out9), .out10(decoder_1_out10), .out11(decoder_1_out11),
    .out12(decoder_1_out12), .out13(decoder_1_out13), .out14(decoder_1_out14), .out15(decoder_1_out15),
    .sel(in_1));  // open: en
  Memory_Cell memory_cell_1 (
    .Read_Address(decoder_1_out0), .in_2(in_4), .Write_Address(decoder_2_out0), .Clock(Clock),
    .out_5(memory_cell_1_out_5), .out_6(out_8));
  Memory_Cell memory_cell_2 (
    .Read_Address(decoder_1_out1), .in_2(in_4), .Write_Address(decoder_2_out1), .Clock(Clock),
    .out_5(memory_cell_2_out_5), .out_6(out_9));
  Memory_Cell memory_cell_3 (
    .Read_Address(decoder_1_out2), .in_2(in_4), .Write_Address(decoder_2_out2), .Clock(Clock),
    .out_5(memory_cell_3_out_5), .out_6(out_10));
  Memory_Cell memory_cell_4 (
    .Read_Address(decoder_1_out3), .in_2(in_4), .Write_Address(decoder_2_out3), .Clock(Clock),
    .out_5(memory_cell_4_out_5), .out_6(out_11));
  Memory_Cell memory_cell_5 (
    .Read_Address(decoder_1_out4), .in_2(in_4), .Write_Address(decoder_2_out4), .Clock(Clock),
    .out_5(memory_cell_5_out_5), .out_6(out_12));
  Memory_Cell memory_cell_6 (
    .Read_Address(decoder_1_out5), .in_2(in_4), .Write_Address(decoder_2_out5), .Clock(Clock),
    .out_5(memory_cell_6_out_5), .out_6(out_13));
  Memory_Cell memory_cell_7 (
    .Read_Address(decoder_1_out6), .in_2(in_4), .Write_Address(decoder_2_out6), .Clock(Clock),
    .out_5(memory_cell_7_out_5), .out_6(out_14));
  Memory_Cell memory_cell_8 (
    .Read_Address(decoder_1_out7), .in_2(in_4), .Write_Address(decoder_2_out7), .Clock(Clock),
    .out_5(memory_cell_8_out_5), .out_6(out_15));
  Memory_Cell memory_cell_9 (
    .Read_Address(decoder_1_out8), .in_2(in_4), .Write_Address(decoder_2_out8), .Clock(Clock),
    .out_5(memory_cell_9_out_5), .out_6(out_16));
  Memory_Cell memory_cell_10 (
    .Read_Address(decoder_1_out9), .in_2(in_4), .Write_Address(decoder_2_out9), .Clock(Clock),
    .out_5(memory_cell_10_out_5), .out_6(out_17));
  Memory_Cell memory_cell_11 (
    .Read_Address(decoder_1_out10), .in_2(in_4), .Write_Address(decoder_2_out10), .Clock(Clock),
    .out_5(memory_cell_11_out_5), .out_6(out_18));
  Memory_Cell memory_cell_12 (
    .Read_Address(decoder_1_out11), .in_2(in_4), .Write_Address(decoder_2_out11), .Clock(Clock),
    .out_5(memory_cell_12_out_5), .out_6(out_19));
  Memory_Cell memory_cell_13 (
    .Read_Address(decoder_1_out12), .in_2(in_4), .Write_Address(decoder_2_out12), .Clock(Clock),
    .out_5(memory_cell_13_out_5), .out_6(out_20));
  Memory_Cell memory_cell_14 (
    .Read_Address(decoder_1_out13), .in_2(in_4), .Write_Address(decoder_2_out13), .Clock(Clock),
    .out_5(memory_cell_14_out_5), .out_6(out_21));
  Memory_Cell memory_cell_15 (
    .Read_Address(decoder_1_out14), .in_2(in_4), .Write_Address(decoder_2_out14), .Clock(Clock),
    .out_5(memory_cell_15_out_5), .out_6(out_22));
  Memory_Cell memory_cell_16 (
    .Read_Address(decoder_1_out15), .in_2(in_4), .Write_Address(decoder_2_out15), .Clock(Clock),
    .out_5(memory_cell_16_out_5), .out_6(out_23));
  assign out_6 = memory_cell_16_out_5 | memory_cell_15_out_5 | memory_cell_14_out_5 | memory_cell_13_out_5 | memory_cell_12_out_5 | memory_cell_11_out_5 | memory_cell_10_out_5 | memory_cell_9_out_5 | memory_cell_8_out_5 | memory_cell_7_out_5 | memory_cell_6_out_5 | memory_cell_5_out_5 | memory_cell_4_out_5 | memory_cell_3_out_5 | memory_cell_2_out_5 | memory_cell_1_out_5;  // OR_Gate or_1, 16 bits wide
  Decoder #(.select(4)) decoder_2 (
    .out0(decoder_2_out0), .out1(decoder_2_out1), .out2(decoder_2_out2), .out3(decoder_2_out3),
    .out4(decoder_2_out4), .out5(decoder_2_out5), .out6(decoder_2_out6), .out7(decoder_2_out7),
    .out8(decoder_2_out8), .out9(decoder_2_out9), .out10(decoder_2_out10), .out11(decoder_2_out11),
    .out12(decoder_2_out12), .out13(decoder_2_out13), .out14(decoder_2_out14), .out15(decoder_2_out15),
    .sel(WA));  // open: en
  Decoder #(.select(4)) decoder_3 (
    .out0(decoder_3_out0), .out1(decoder_3_out1), .out2(decoder_3_out2), .out3(decoder_3_out3),
    .out4(decoder_3_out4), .out5(decoder_3_out5), .out6(decoder_3_out6), .out7(decoder_3_out7),
    .out8(decoder_3_out8), .out9(decoder_3_out9), .out10(decoder_3_out10), .out11(decoder_3_out11),
    .out12(decoder_3_out12), .out13(decoder_3_out13), .out14(decoder_3_out14), .out15(decoder_3_out15),
    .sel(in_2));  // open: en
  Memory_Cell memory_cell_17 (
    .Read_Address(decoder_3_out0), .in_2(in_4), .Write_Address(decoder_2_out0), .Clock(Clock),
    .out_5(memory_cell_17_out_5));  // open: out_6
  Memory_Cell memory_cell_18 (
    .Read_Address(decoder_3_out1), .in_2(in_4), .Write_Address(decoder_2_out1), .Clock(Clock),
    .out_5(memory_cell_18_out_5));  // open: out_6
  Memory_Cell memory_cell_19 (
    .Read_Address(decoder_3_out2), .in_2(in_4), .Write_Address(decoder_2_out2), .Clock(Clock),
    .out_5(memory_cell_19_out_5));  // open: out_6
  Memory_Cell memory_cell_20 (
    .Read_Address(decoder_3_out3), .in_2(in_4), .Write_Address(decoder_2_out3), .Clock(Clock),
    .out_5(memory_cell_20_out_5));  // open: out_6
  Memory_Cell memory_cell_21 (
    .Read_Address(decoder_3_out4), .in_2(in_4), .Write_Address(decoder_2_out4), .Clock(Clock),
    .out_5(memory_cell_21_out_5));  // open: out_6
  Memory_Cell memory_cell_22 (
    .Read_Address(decoder_3_out5), .in_2(in_4), .Write_Address(decoder_2_out5), .Clock(Clock),
    .out_5(memory_cell_22_out_5));  // open: out_6
  Memory_Cell memory_cell_23 (
    .Read_Address(decoder_3_out6), .in_2(in_4), .Write_Address(decoder_2_out6), .Clock(Clock),
    .out_5(memory_cell_23_out_5));  // open: out_6
  Memory_Cell memory_cell_24 (
    .Read_Address(decoder_3_out7), .in_2(in_4), .Write_Address(decoder_2_out7), .Clock(Clock),
    .out_5(memory_cell_24_out_5));  // open: out_6
  Memory_Cell memory_cell_25 (
    .Read_Address(decoder_3_out8), .in_2(in_4), .Write_Address(decoder_2_out8), .Clock(Clock),
    .out_5(memory_cell_25_out_5));  // open: out_6
  Memory_Cell memory_cell_26 (
    .Read_Address(decoder_3_out9), .in_2(in_4), .Write_Address(decoder_2_out9), .Clock(Clock),
    .out_5(memory_cell_26_out_5));  // open: out_6
  Memory_Cell memory_cell_27 (
    .Read_Address(decoder_3_out10), .in_2(in_4), .Write_Address(decoder_2_out10), .Clock(Clock),
    .out_5(memory_cell_27_out_5));  // open: out_6
  Memory_Cell memory_cell_28 (
    .Read_Address(decoder_3_out11), .in_2(in_4), .Write_Address(decoder_2_out11), .Clock(Clock),
    .out_5(memory_cell_28_out_5));  // open: out_6
  Memory_Cell memory_cell_29 (
    .Read_Address(decoder_3_out12), .in_2(in_4), .Write_Address(decoder_2_out12), .Clock(Clock),
    .out_5(memory_cell_29_out_5));  // open: out_6
  Memory_Cell memory_cell_30 (
    .Read_Address(decoder_3_out13), .in_2(in_4), .Write_Address(decoder_2_out13), .Clock(Clock),
    .out_5(memory_cell_30_out_5));  // open: out_6
  Memory_Cell memory_cell_31 (
    .Read_Address(decoder_3_out14), .in_2(in_4), .Write_Address(decoder_2_out14), .Clock(Clock),
    .out_5(memory_cell_31_out_5));  // open: out_6
  Memory_Cell memory_cell_32 (
    .Read_Address(decoder_3_out15), .in_2(in_4), .Write_Address(decoder_2_out15), .Clock(Clock),
    .out_5(memory_cell_32_out_5));  // open: out_6
  assign out_7 = memory_cell_32_out_5 | memory_cell_31_out_5 | memory_cell_30_out_5 | memory_cell_29_out_5 | memory_cell_28_out_5 | memory_cell_17_out_5 | memory_cell_27_out_5 | memory_cell_26_out_5 | memory_cell_25_out_5 | memory_cell_24_out_5 | memory_cell_23_out_5 | memory_cell_22_out_5 | memory_cell_21_out_5 | memory_cell_20_out_5 | memory_cell_19_out_5 | memory_cell_18_out_5;  // OR_Gate or_2, 16 bits wide

  // Other names for the same wires on the sheet: R0[15:0] = out_8; R1[15:0] = out_9; R2[15:0] = out_10;
  //   R3[15:0] = out_11; R4[15:0] = out_12; R5[15:0] = out_13; R6[15:0] = out_14; R7[15:0] = out_15;
  //   R8[15:0] = out_16; R9[15:0] = out_17; R10[15:0] = out_18; R11[15:0] = out_19; R12[15:0] = out_20;
  //   R13[15:0] = out_21; R14[15:0] = out_22; R15[15:0] = out_23

  // Notes on the sheet:
  //   RA
  //   WD
  //   RA1
  //   RD1
  //   RA2
  //   RD2
endmodule

module Memory_Cell (
  input  Read_Address,
  input  [15:0] in_2,
  input  Write_Address,
  input  Clock,
  output [15:0] out_5,
  output [15:0] out_6
);

  Register #(.width(16)) register_1 (.D(in_2), .en(Write_Address), .Q(out_6), .clk(Clock));  // open: clr
  Multiplexer #(.width(16)) multiplexer_1 (.in0({16{1'b0}}), .in1(out_6), .out(out_5), .sel(Read_Address));  // open: en

  // Notes on the sheet:
  //   Write Data
  //   Read Data
  //   output
endmodule

module Flags (
  input  [4:0] in_1,
  input  Clock,
  output [4:0] out_3
);

  Register #(.width(5)) register_1 (.D(in_1), .Q(out_3), .clk(Clock));  // open: en, clr

  // Notes on the sheet:
  //   Current Flags
  //   New Flags
endmodule

module Branching_Control (
  input  [15:0] in_1,
  input  [7:0] in_2,
  input  [4:0] BCVZS,
  input  [15:0] in_4,
  input  in_5,
  input  [3:0] in_6,
  output [15:0] out_7
);

  wire not_1_out, or_1_out, or_2_out, xor_1_out, xor_2_out;
  wire [15:0] adder_1_out, adder_2_out, bit_extender_1_out, bit_extender_2_out, multiplexer_1_out,
       multiplexer_2_out, multiplexer_3_out, multiplexer_4_out, multiplexer_5_out, multiplexer_6_out,
       multiplexer_7_out, multiplexer_8_out, multiplexer_9_out, multiplexer_10_out, multiplexer_11_out,
       multiplexer_12_out, multiplexer_13_out, multiplexer_14_out, multiplexer_15_out, multiplexer_16_out,
       multiplexer_17_out, multiplexer_18_out, multiplexer_19_out, multiplexer_20_out, multiplexer_21_out,
       multiplexer_22_out, multiplexer_23_out, multiplexer_24_out, multiplexer_25_out, multiplexer_26_out,
       multiplexer_27_out, multiplexer_28_out, multiplexer_29_out, multiplexer_30_out;

  assign bit_extender_1_out = {{8{1'b0}}, in_2};  // Bit_Extender bit_extender_1
  Adder #(.width(16)) adder_1 (.a(in_1), .b(bit_extender_1_out), .out(adder_1_out));  // open: cin, cout
  Adder #(.width(16)) adder_2 (.a(in_1), .b(16'h1), .out(adder_2_out));  // open: cin, cout
  xor xor_1 (xor_1_out, BCVZS[2], BCVZS[0]);
  not not_1 (not_1_out, BCVZS[3]);
  xor xor_2 (xor_2_out, BCVZS[2], BCVZS[0]);
  or or_1 (or_1_out, xor_1_out, BCVZS[1]);
  or or_2 (or_2_out, not_1_out, BCVZS[1]);
  Multiplexer #(.width(16)) multiplexer_1 (
    .in0(adder_2_out), .in1(in_4), .out(multiplexer_1_out), .sel(xor_1_out));  // open: en
  Multiplexer #(.width(16)) multiplexer_2 (
    .in0(in_4), .in1(adder_2_out), .out(multiplexer_2_out), .sel(xor_1_out));  // open: en
  Multiplexer #(.width(16)) multiplexer_3 (
    .in0(adder_2_out), .in1(in_4), .out(multiplexer_3_out), .sel(or_1_out));  // open: en
  Multiplexer #(.width(16)) multiplexer_4 (
    .in0(in_4), .in1(adder_2_out), .out(multiplexer_4_out), .sel(or_1_out));  // open: en
  Multiplexer #(.width(16)) multiplexer_5 (
    .in0(adder_2_out), .in1(in_4), .out(multiplexer_5_out), .sel(or_2_out));  // open: en
  Multiplexer #(.width(16)) multiplexer_6 (
    .in0(in_4), .in1(adder_2_out), .out(multiplexer_6_out), .sel(or_2_out));  // open: en
  Multiplexer #(.width(16)) multiplexer_7 (
    .in0(adder_2_out), .in1(in_4), .out(multiplexer_7_out), .sel(BCVZS[1]));  // open: en
  Multiplexer #(.width(16)) multiplexer_8 (
    .in0(in_4), .in1(adder_2_out), .out(multiplexer_8_out), .sel(BCVZS[1]));  // open: en
  Multiplexer #(.width(16)) multiplexer_9 (
    .in0(adder_2_out), .in1(in_4), .out(multiplexer_9_out), .sel(BCVZS[3]));  // open: en
  Multiplexer #(.width(16)) multiplexer_10 (
    .in0(in_4), .in1(adder_2_out), .out(multiplexer_10_out), .sel(BCVZS[3]));  // open: en
  Multiplexer #(.width(16)) multiplexer_11 (
    .in0(adder_2_out), .in1(in_4), .out(multiplexer_11_out), .sel(BCVZS[0]));  // open: en
  Multiplexer #(.width(16)) multiplexer_12 (
    .in0(in_4), .in1(adder_2_out), .out(multiplexer_12_out), .sel(BCVZS[0]));  // open: en
  Multiplexer #(.width(16)) multiplexer_13 (
    .in0(adder_2_out), .in1(in_4), .out(multiplexer_13_out), .sel(BCVZS[2]));  // open: en
  Multiplexer #(.width(16)) multiplexer_14 (
    .in0(in_4), .in1(adder_2_out), .out(multiplexer_14_out), .sel(BCVZS[2]));  // open: en
  Multiplexer #(.width(16)) multiplexer_15 (
    .in0(adder_2_out), .in1(bit_extender_2_out), .out(multiplexer_15_out), .sel(xor_2_out));  // open: en
  Multiplexer #(.width(16)) multiplexer_16 (
    .in0(bit_extender_2_out), .in1(adder_2_out), .out(multiplexer_16_out), .sel(xor_2_out));  // open: en
  Multiplexer #(.width(16)) multiplexer_17 (
    .in0(adder_2_out), .in1(bit_extender_2_out), .out(multiplexer_17_out), .sel(or_1_out));  // open: en
  Multiplexer #(.width(16)) multiplexer_18 (
    .in0(bit_extender_2_out), .in1(adder_2_out), .out(multiplexer_18_out), .sel(or_1_out));  // open: en
  Multiplexer #(.width(16)) multiplexer_19 (
    .in0(adder_2_out), .in1(bit_extender_2_out), .out(multiplexer_19_out), .sel(or_2_out));  // open: en
  Multiplexer #(.width(16)) multiplexer_20 (
    .in0(bit_extender_2_out), .in1(adder_2_out), .out(multiplexer_20_out), .sel(or_2_out));  // open: en
  Multiplexer #(.width(16)) multiplexer_21 (
    .in0(adder_2_out), .in1(bit_extender_2_out), .out(multiplexer_21_out), .sel(BCVZS[1]));  // open: en
  Multiplexer #(.width(16)) multiplexer_22 (
    .in0(bit_extender_2_out), .in1(adder_2_out), .out(multiplexer_22_out), .sel(BCVZS[1]));  // open: en
  Multiplexer #(.width(16)) multiplexer_23 (
    .in0(adder_2_out), .in1(bit_extender_2_out), .out(multiplexer_23_out), .sel(BCVZS[3]));  // open: en
  Multiplexer #(.width(16)) multiplexer_24 (
    .in0(bit_extender_2_out), .in1(adder_2_out), .out(multiplexer_24_out), .sel(BCVZS[3]));  // open: en
  Multiplexer #(.width(16)) multiplexer_25 (
    .in0(adder_2_out), .in1(bit_extender_2_out), .out(multiplexer_25_out), .sel(BCVZS[0]));  // open: en
  Multiplexer #(.width(16)) multiplexer_26 (
    .in0(bit_extender_2_out), .in1(adder_2_out), .out(multiplexer_26_out), .sel(BCVZS[0]));  // open: en
  Multiplexer #(.width(16)) multiplexer_27 (
    .in0(adder_2_out), .in1(bit_extender_2_out), .out(multiplexer_27_out), .sel(BCVZS[2]));  // open: en
  Multiplexer #(.width(16)) multiplexer_28 (
    .in0(bit_extender_2_out), .in1(adder_2_out), .out(multiplexer_28_out), .sel(BCVZS[2]));  // open: en
  assign bit_extender_2_out = {{8{1'b0}}, adder_1_out[7:0]};  // Bit_Extender bit_extender_2
  Multiplexer #(.select(4), .width(16)) multiplexer_29 (
    .in0(in_4), .in2(multiplexer_1_out), .in3(multiplexer_2_out), .in4(multiplexer_3_out),
    .in5(multiplexer_4_out), .in6(multiplexer_5_out), .in7(multiplexer_6_out), .in8(multiplexer_7_out),
    .in9(multiplexer_8_out), .in10(multiplexer_9_out), .in11(multiplexer_10_out), .in12(multiplexer_11_out),
    .in13(multiplexer_12_out), .in14(multiplexer_13_out), .in15(multiplexer_14_out),
    .out(multiplexer_29_out), .sel(in_6));  // open: in1, en
  Multiplexer #(.select(4), .width(16)) multiplexer_30 (
    .in0(bit_extender_2_out), .in2(multiplexer_15_out), .in3(multiplexer_16_out), .in4(multiplexer_17_out),
    .in5(multiplexer_18_out), .in6(multiplexer_19_out), .in7(multiplexer_20_out), .in8(multiplexer_21_out),
    .in9(multiplexer_22_out), .in10(multiplexer_23_out), .in11(multiplexer_24_out),
    .in12(multiplexer_25_out), .in13(multiplexer_26_out), .in14(multiplexer_27_out),
    .in15(multiplexer_28_out), .out(multiplexer_30_out), .sel(in_6));  // open: in1, en
  Multiplexer #(.width(16)) multiplexer_31 (
    .in0(multiplexer_29_out), .in1(multiplexer_30_out), .out(out_7), .sel(in_5));  // open: en

  // Notes on the sheet:
  //   Current value of PC
  //   o
  //   Flags
  //   RD R11 from Reg file
  //   relative branch
  //   Branch Op Select
  //   relative
  //   New Value of PC
endmodule

module Operation_Control (
  input  [15:0] in_1,
  output HALT,
  output [3:0] out_3,
  output [3:0] out_4,
  output [3:0] out_5,
  output [3:0] Source_2,
  output [7:0] out_7,
  output out_8,
  output out_9,
  output [3:0] out_10,
  output [5:0] out_11,
  output out_12,
  output [3:0] out_13,
  output out_14,
  output [2:0] out_15,
  output [4:0] out_16,
  output out_17,
  output out_18,
  output relative_branch,
  output STORE,
  output out_21,
  output out_22,
  output [4:0] out_23,
  output [3:0] Rd,
  output [3:0] Rb,
  output out_26
);

  wire comparator_2_eq, comparator_3_eq, comparator_4_eq, comparator_8_eq, comparator_10_eq, or_1_out;

  Comparator #(.width(16)) comparator_1 (.a(in_1), .b({16{1'b0}}), .eq(HALT));  // open: gt, lt
  Comparator #(.width(5)) comparator_2 (
    .a({in_1[15:12], in_1[7]}), .b(5'b00111), .eq(comparator_2_eq));  // open: gt, lt
  Comparator comparator_3 (.a(in_1[15:8]), .b(8'h20), .eq(comparator_3_eq));  // open: gt, lt
  Comparator comparator_4 (.a(in_1[15:8]), .b(8'h21), .eq(comparator_4_eq));  // open: gt, lt
  Comparator comparator_5 (.a({in_1[15:12], in_1[7:4]}), .b(8'h36), .eq(out_14));  // open: gt, lt
  Comparator #(.width(3)) comparator_6 (.a(in_1[15:13]), .b(3'b011), .eq(STORE));  // open: gt, lt
  Comparator #(.width(3)) comparator_7 (.a(in_1[15:13]), .b(3'b010), .eq(out_21));  // open: gt, lt
  Multiplexer #(.width(4)) multiplexer_1 (
    .in0(in_1[3:0]), .in1(in_1[11:8]), .out(Source_2), .sel(or_1_out));  // open: en
  or or_1 (or_1_out, comparator_2_eq, out_9);
  Comparator #(.width(4)) comparator_8 (.a(in_1[15:12]), .b(4'b1110), .eq(comparator_8_eq));  // open: gt, lt
  Comparator #(.width(4)) comparator_9 (.a(in_1[15:12]), .b(4'b1111), .eq(out_8));  // open: gt, lt
  Comparator #(.width(4)) comparator_10 (.a(in_1[15:12]), .b(4'b0001), .eq(comparator_10_eq));  // open: gt, lt
  Comparator #(.width(4)) comparator_11 (.a(in_1[15:12]), .b(4'b0000), .eq(relative_branch));  // open: gt, lt
  Comparator #(.width(12)) comparator_12 (.a({in_1[15:12], in_1[7:0]}), .b(12'h370), .eq(out_17));  // open: gt, lt
  Comparator #(.width(12)) comparator_13 (.a({in_1[15:12], in_1[7:0]}), .b(12'h378), .eq(out_18));  // open: gt, lt
  or or_2 (out_9, comparator_8_eq, out_8);
  or or_3 (out_22, STORE, out_21);
  Multiplexer #(.width(4)) multiplexer_2 (.in0(in_1[7:4]), .in1(in_1[11:8]), .out(out_5), .sel(out_18));  // open: en
  or or_4 (out_12, comparator_3_eq, comparator_10_eq, relative_branch, comparator_4_eq);
  or or_5 (out_26, comparator_4_eq, comparator_3_eq);

  assign out_3 = in_1[15:12];
  assign out_4 = in_1[11:8];
  assign out_7 = in_1[7:0];
  assign out_10 = in_1[7:4];
  assign out_11 = in_1[5:0];
  assign out_13 = in_1[11:8];
  assign out_15 = in_1[11:9];
  assign out_16 = {in_1[8], in_1[3:0]};
  assign out_23 = {in_1[12], in_1[7:4]};
  assign Rb = in_1[3:0];
  assign Rd = in_1[11:8];

  // Notes on the sheet:
  //   destination
  //   Op Select
  //   Source 1
  //   v
  //   Register Adresses
  //   Is SETHI op ?
  //   SET op
  //   Shift OP Select
  //   Inc/Dec
  //   Is Branch Op/CALL/RETURN
  //   Branch Op Select
  //   Is flag op
  //   flag Op
  //   Flags v4 v3 v2 v1 v0
  //   Save
  //   Restore
  //   LOAD
  //   Memory
  //   Offset
  //   IS CALL/RETURN
endmodule

module A (
  input  [15:0] in_1,
  input  [4:0] in_2,
  output [4:0] out_3
);

  Comparator #(.width(16)) comparator_1 (.a(in_1), .b({16{1'b0}}), .eq(out_3[1]));  // open: gt, lt

  assign {out_3[4:2], out_3[0]} = {in_2[4:2], in_1[15]};

  // Notes on the sheet:
  //   BCVZS
  //   BCVZS
endmodule

module Call_Return (
  input  [15:0] in_1,
  input  [15:0] in_2,
  input  [15:0] in_3,
  input  [15:0] in_4,
  output [15:0] out_5,
  output [15:0] out_6,
  output [15:0] out_7,
  output [15:0] out_8
);

  Adder #(.width(16)) adder_1 (.a(in_1), .b(16'h1), .out(out_6));  // open: cin, cout

  assign out_5 = in_2;
  assign out_7 = in_4;
  assign out_8 = in_3;

  // Notes on the sheet:
  //   PC
  //   R13
  //   R14
  //   R12
  //   PC
  //   R13
  //   R14
  //   R12
endmodule

module B (
  input  [3:0] in_1,
  input  [3:0] in_2,
  input  [3:0] in_3,
  input  [15:0] in_4,
  input  [15:0] in_5,
  input  [15:0] in_6,
  input  in_7,
  input  in_8,
  output [3:0] out_9,
  output [15:0] out_10,
  output out_11
);

  wire not_1_out;
  wire [1:0] counter_1_q;

  not not_1 (not_1_out, in_8);
  Multiplexer #(.select(2), .width(4)) multiplexer_1 (
    .in0(in_1), .in1(in_2), .in2(in_3), .out(out_9), .sel(counter_1_q));  // open: in3, en
  Multiplexer #(.select(2), .width(16)) multiplexer_2 (
    .in0(in_4), .in1(in_5), .in2(in_6), .out(out_10), .sel(counter_1_q));  // open: in3, en
  Counter #(.width(2), .max('h3)) counter_1 (
    .Q(counter_1_q), .clk(in_7), .clr(not_1_out));  // open: load, D, count, carry
  Comparator #(.width(2)) comparator_1 (.a(counter_1_q), .b(2'b10), .eq(out_11));  // open: gt, lt

  // Notes on the sheet:
  //   WA1
  //   WA2
  //   WA3
  //   WD1
  //   WD2
  //   WD3
  //   clock
  //   WA
  //   WD
endmodule
