// Logisim project Vending_machine.circ as structural Verilog: 1 circuit, main circuit main
module main (
  input  Q,
  input  D0,
  input  D1,
  input  D2,
  output V,
  output N0,
  output N1,
  output N2
);

  wire comparator_1_eq, comparator_1_gt;
  wire [1:0] bitadder_1_out;
  wire [5:0] adder_1_out, adder_2_out, bit_extender_1_out, bit_extender_2_out, multiplier_1_out,
       multiplier_2_out, multiplier_3_out, multiplier_4_out, subtractor_1_out;
  wire [5:3] multiplexer_1_out;

  assign bit_extender_1_out = {{5{1'b0}}, Q};  // Bit_Extender bit_extender_1
  BitAdder #(.width(1)) bitadder_1 (.in0(D0), .in1(D1), .in2(D2), .out(bitadder_1_out));
  assign bit_extender_2_out = {{4{1'b0}}, bitadder_1_out};  // Bit_Extender bit_extender_2
  Multiplier #(.width(6)) multiplier_1 (
    .a(bit_extender_1_out), .b(6'b000101), .out(multiplier_1_out));  // open: cin, cout
  Multiplier #(.width(6)) multiplier_2 (
    .a(bit_extender_2_out), .b(6'b000010), .out(multiplier_2_out));  // open: cin, cout
  Multiplier #(.width(6)) multiplier_3 (
    .a(bit_extender_1_out), .b(6'b011001), .out(multiplier_3_out));  // open: cin, cout
  Multiplier #(.width(6)) multiplier_4 (
    .a(bit_extender_2_out), .b(6'b001010), .out(multiplier_4_out));  // open: cin, cout
  Adder #(.width(6)) adder_1 (.a(multiplier_1_out), .b(multiplier_2_out), .out(adder_1_out));  // open: cin, cout
  Adder #(.width(6)) adder_2 (.a(multiplier_3_out), .b(multiplier_4_out), .out(adder_2_out));  // open: cin, cout
  Subtractor #(.width(6)) subtractor_1 (.a(adder_1_out), .b(6'b000110), .out(subtractor_1_out));  // open: bin, bout
  Comparator #(.width(6), .mode("unsigned")) comparator_1 (
    .a(adder_2_out), .b(6'b011110), .gt(comparator_1_gt), .eq(comparator_1_eq));  // open: lt
  Multiplexer #(.width(6)) multiplexer_1 (
    .in0(adder_1_out), .in1(subtractor_1_out), .out({multiplexer_1_out, N0, N1, N2}), .sel(V));  // open: en
  or or_1 (V, comparator_1_gt, comparator_1_eq);
endmodule
